// Logisim project logisim_Pong.circ as structural Verilog: 5 circuits, main circuit main
module main (
  input  Start
);

  wire boarder_checker_1_hit_boarder, boarder_checker_1_nearpaddle_left, boarder_checker_1_nearpaddle_right,
       CLK_out, Down_2_out, Down_out, hit_out, or_1_out, Paddle_Left_hit, Paddle_Right_hit, UP_2_out, UP_out;
  wire [15:0] ball_y_1_out, multiplexer_1_out, multiplexer_2_out, multiplexer_3_out, multiplexer_4_out,
       multiplexer_5_out, multiplexer_6_out, multiplexer_7_out, multiplexer_8_out, multiplexer_9_out,
       multiplexer_10_out, multiplexer_11_out, multiplexer_12_out, multiplexer_13_out, multiplexer_14_out,
       multiplexer_15_out, multiplexer_16_out, multiplexer_17_out, multiplexer_18_out, multiplexer_19_out,
       multiplexer_20_out, multiplexer_21_out, multiplexer_22_out, multiplexer_23_out, multiplexer_24_out,
       multiplexer_25_out, multiplexer_26_out, multiplexer_27_out, multiplexer_28_out, multiplexer_29_out,
       multiplexer_30_out, multiplexer_31_out, multiplexer_32_out, or_2_out, or_3_out, Paddle_Left_out,
       Paddle_Right_out;
  wire [31:0] ball_x_1_out;

  Clock CLK (.out(CLK_out));
  or or_1 (or_1_out, boarder_checker_1_hit_boarder, Start);
  Button UP (.out(UP_out));
  Button Down (.out(Down_out));
  Ball_Y ball_y_1 (.Out(ball_y_1_out), .Reset(or_1_out), .Clk(CLK_out), .hit(hit_out));
  Ball_X ball_x_1 (.Reset(or_1_out), .Clk(CLK_out), .Out(ball_x_1_out), .hit(hit_out));
  or hit (hit_out, Paddle_Left_hit, Paddle_Right_hit);
  Paddle_1 Paddle_Left (
    .Button_Down(Down_out), .Button_UP(UP_out), .Reset(or_1_out), .Ball_y(ball_y_1_out),
    .Out(Paddle_Left_out), .Hit(Paddle_Left_hit), .NearPAddle(boarder_checker_1_nearpaddle_left));
  Multiplexer #(.width(16), .enable("false")) multiplexer_1 (
    .in0({16{1'b0}}), .in1(ball_y_1_out), .out(multiplexer_1_out), .sel(ball_x_1_out[0]));
  Boarder_checker boarder_checker_1 (
    .Ball_X(ball_x_1_out), .Hit_Boarder(boarder_checker_1_hit_boarder),
    .NearPaddle_Right(boarder_checker_1_nearpaddle_right), .NearPaddle_Left(boarder_checker_1_nearpaddle_left));
  assign or_2_out = Paddle_Left_out | multiplexer_1_out;  // OR_Gate or_2, 16 bits wide
  Multiplexer #(.width(16), .enable("false")) multiplexer_2 (
    .in0({16{1'b0}}), .in1(ball_y_1_out), .out(multiplexer_2_out), .sel(ball_x_1_out[1]));
  Multiplexer #(.width(16), .enable("false")) multiplexer_3 (
    .in0({16{1'b0}}), .in1(ball_y_1_out), .out(multiplexer_3_out), .sel(ball_x_1_out[3]));
  Multiplexer #(.width(16), .enable("false")) multiplexer_4 (
    .in0({16{1'b0}}), .in1(ball_y_1_out), .out(multiplexer_4_out), .sel(ball_x_1_out[2]));
  Multiplexer #(.width(16), .enable("false")) multiplexer_5 (
    .in0({16{1'b0}}), .in1(ball_y_1_out), .out(multiplexer_5_out), .sel(ball_x_1_out[4]));
  Multiplexer #(.width(16), .enable("false")) multiplexer_6 (
    .in0({16{1'b0}}), .in1(ball_y_1_out), .out(multiplexer_6_out), .sel(ball_x_1_out[5]));
  DotMatrix #(.matrixcols(32), .matrixrows(16)) dotmatrix_1 (
    .col0(or_2_out), .col1(multiplexer_2_out), .col2(multiplexer_4_out), .col3(multiplexer_3_out),
    .col4(multiplexer_5_out), .col5(multiplexer_6_out), .col6(multiplexer_7_out), .col7(multiplexer_9_out),
    .col8(multiplexer_8_out), .col9(multiplexer_10_out), .col10(multiplexer_12_out),
    .col11(multiplexer_11_out), .col12(multiplexer_13_out), .col13(multiplexer_14_out),
    .col14(multiplexer_15_out), .col15(multiplexer_16_out), .col16(multiplexer_17_out),
    .col17(multiplexer_18_out), .col18(multiplexer_20_out), .col19(multiplexer_19_out),
    .col20(multiplexer_22_out), .col21(multiplexer_21_out), .col22(multiplexer_23_out),
    .col23(multiplexer_25_out), .col24(multiplexer_24_out), .col25(multiplexer_26_out),
    .col26(multiplexer_28_out), .col27(multiplexer_27_out), .col28(multiplexer_30_out),
    .col29(multiplexer_29_out), .col30(multiplexer_31_out), .col31(or_3_out));
  Multiplexer #(.width(16), .enable("false")) multiplexer_7 (
    .in0({16{1'b0}}), .in1(ball_y_1_out), .out(multiplexer_7_out), .sel(ball_x_1_out[6]));
  Multiplexer #(.width(16), .enable("false")) multiplexer_8 (
    .in0({16{1'b0}}), .in1(ball_y_1_out), .out(multiplexer_8_out), .sel(ball_x_1_out[8]));
  Multiplexer #(.width(16), .enable("false")) multiplexer_9 (
    .in0({16{1'b0}}), .in1(ball_y_1_out), .out(multiplexer_9_out), .sel(ball_x_1_out[7]));
  Multiplexer #(.width(16), .enable("false")) multiplexer_10 (
    .in0({16{1'b0}}), .in1(ball_y_1_out), .out(multiplexer_10_out), .sel(ball_x_1_out[9]));
  Button UP_2 (.out(UP_2_out));
  Button Down_2 (.out(Down_2_out));
  Multiplexer #(.width(16), .enable("false")) multiplexer_11 (
    .in0({16{1'b0}}), .in1(ball_y_1_out), .out(multiplexer_11_out), .sel(ball_x_1_out[11]));
  Multiplexer #(.width(16), .enable("false")) multiplexer_12 (
    .in0({16{1'b0}}), .in1(ball_y_1_out), .out(multiplexer_12_out), .sel(ball_x_1_out[10]));
  Multiplexer #(.width(16), .enable("false")) multiplexer_13 (
    .in0({16{1'b0}}), .in1(ball_y_1_out), .out(multiplexer_13_out), .sel(ball_x_1_out[12]));
  Multiplexer #(.width(16), .enable("false")) multiplexer_14 (
    .in0({16{1'b0}}), .in1(ball_y_1_out), .out(multiplexer_14_out), .sel(ball_x_1_out[13]));
  Multiplexer #(.width(16), .enable("false")) multiplexer_15 (
    .in0({16{1'b0}}), .in1(ball_y_1_out), .out(multiplexer_15_out), .sel(ball_x_1_out[14]));
  Multiplexer #(.width(16), .enable("false")) multiplexer_16 (
    .in0({16{1'b0}}), .in1(ball_y_1_out), .out(multiplexer_16_out), .sel(ball_x_1_out[15]));
  Multiplexer #(.width(16), .enable("false")) multiplexer_17 (
    .in0({16{1'b0}}), .in1(ball_y_1_out), .out(multiplexer_17_out), .sel(ball_x_1_out[16]));
  Multiplexer #(.width(16), .enable("false")) multiplexer_18 (
    .in0({16{1'b0}}), .in1(ball_y_1_out), .out(multiplexer_18_out), .sel(ball_x_1_out[17]));
  Paddle_1 Paddle_Right (
    .Button_Down(UP_2_out), .Button_UP(Down_2_out), .Reset(or_1_out), .Ball_y(ball_y_1_out),
    .Out(Paddle_Right_out), .Hit(Paddle_Right_hit), .NearPAddle(boarder_checker_1_nearpaddle_right));
  Multiplexer #(.width(16), .enable("false")) multiplexer_19 (
    .in0({16{1'b0}}), .in1(ball_y_1_out), .out(multiplexer_19_out), .sel(ball_x_1_out[19]));
  Multiplexer #(.width(16), .enable("false")) multiplexer_20 (
    .in0({16{1'b0}}), .in1(ball_y_1_out), .out(multiplexer_20_out), .sel(ball_x_1_out[18]));
  Multiplexer #(.width(16), .enable("false")) multiplexer_21 (
    .in0({16{1'b0}}), .in1(ball_y_1_out), .out(multiplexer_21_out), .sel(ball_x_1_out[21]));
  Multiplexer #(.width(16), .enable("false")) multiplexer_22 (
    .in0({16{1'b0}}), .in1(ball_y_1_out), .out(multiplexer_22_out), .sel(ball_x_1_out[20]));
  assign or_3_out = Paddle_Right_out | multiplexer_32_out;  // OR_Gate or_3, 16 bits wide
  Multiplexer #(.width(16), .enable("false")) multiplexer_23 (
    .in0({16{1'b0}}), .in1(ball_y_1_out), .out(multiplexer_23_out), .sel(ball_x_1_out[22]));
  Multiplexer #(.width(16), .enable("false")) multiplexer_24 (
    .in0({16{1'b0}}), .in1(ball_y_1_out), .out(multiplexer_24_out), .sel(ball_x_1_out[24]));
  Multiplexer #(.width(16), .enable("false")) multiplexer_25 (
    .in0({16{1'b0}}), .in1(ball_y_1_out), .out(multiplexer_25_out), .sel(ball_x_1_out[23]));
  Multiplexer #(.width(16), .enable("false")) multiplexer_26 (
    .in0({16{1'b0}}), .in1(ball_y_1_out), .out(multiplexer_26_out), .sel(ball_x_1_out[25]));
  Multiplexer #(.width(16), .enable("false")) multiplexer_27 (
    .in0({16{1'b0}}), .in1(ball_y_1_out), .out(multiplexer_27_out), .sel(ball_x_1_out[27]));
  Multiplexer #(.width(16), .enable("false")) multiplexer_28 (
    .in0({16{1'b0}}), .in1(ball_y_1_out), .out(multiplexer_28_out), .sel(ball_x_1_out[26]));
  Multiplexer #(.width(16), .enable("false")) multiplexer_29 (
    .in0({16{1'b0}}), .in1(ball_y_1_out), .out(multiplexer_29_out), .sel(ball_x_1_out[29]));
  Multiplexer #(.width(16), .enable("false")) multiplexer_30 (
    .in0({16{1'b0}}), .in1(ball_y_1_out), .out(multiplexer_30_out), .sel(ball_x_1_out[28]));
  Multiplexer #(.width(16), .enable("false")) multiplexer_31 (
    .in0({16{1'b0}}), .in1(ball_y_1_out), .out(multiplexer_31_out), .sel(ball_x_1_out[30]));
  Multiplexer #(.width(16), .enable("false")) multiplexer_32 (
    .in0({16{1'b0}}), .in1(ball_y_1_out), .out(multiplexer_32_out), .sel(ball_x_1_out[31]));
endmodule

module Ball_X (
  input  hit,
  input  Reset,
  input  Clk,
  output [31:0] Out
);

  wire comparator_1_eq, comparator_2_eq, multiplexer_1_out, not_1_out, or_1_out, register_1_q;
  wire [0:0] xor_1_out;
  wire [4:0] adder_1_out, multiplexer_2_out, register_2_q, subtractor_1_out;

  Multiplexer #(.enable("false")) multiplexer_1 (.in0(not_1_out), .in1(1'b1), .out(multiplexer_1_out), .sel(Reset));
  not not_1 (not_1_out, register_1_q);
  Register #(.width(1)) register_1 (.D(multiplexer_1_out), .en(or_1_out), .Q(register_1_q), .clk(Clk), .clr(Reset));
  Multiplexer #(.select(2), .width(5), .enable("false")) multiplexer_2 (
    .in0(adder_1_out), .in1(subtractor_1_out), .in2(5'b01010), .in3(5'b01010), .out(multiplexer_2_out),
    .sel({Reset, xor_1_out[0]}));
  xor xor_1 (xor_1_out[0], register_1_q, or_1_out);
  Register #(.width(5)) register_2 (.D(multiplexer_2_out), .en(1'b1), .Q(register_2_q), .clk(Clk));  // open: clr
  Subtractor #(.width(5)) subtractor_1 (.a(register_2_q), .b(5'b00001), .out(subtractor_1_out));  // open: bin, bout
  Adder #(.width(5)) adder_1 (.a(register_2_q), .b(5'b00001), .out(adder_1_out));  // open: cin, cout
  or or_1 (or_1_out, comparator_2_eq, hit, comparator_1_eq);
  Comparator #(.width(5)) comparator_1 (.a({5{1'b1}}), .b(register_2_q), .eq(comparator_1_eq));  // open: gt, lt
  Comparator #(.width(5)) comparator_2 (.a({5{1'b0}}), .b(register_2_q), .eq(comparator_2_eq));  // open: gt, lt
  Shifter #(.width(32)) shifter_1 (.in(32'h1), .\dist (register_2_q), .out(Out));
endmodule

module Ball_Y (
  input  Reset,
  input  Clk,
  input  hit,
  output [15:0] Out
);

  wire comparator_1_eq, comparator_2_eq, multiplexer_1_out, not_1_out, or_1_out, register_1_q;
  wire [0:0] xor_1_out;
  wire [3:0] adder_1_out, multiplexer_2_out, register_2_q, subtractor_1_out;

  Multiplexer #(.enable("false")) multiplexer_1 (.in0(not_1_out), .in1(1'b1), .out(multiplexer_1_out), .sel(Reset));
  not not_1 (not_1_out, register_1_q);
  Register #(.width(1)) register_1 (.D(multiplexer_1_out), .en(or_1_out), .Q(register_1_q), .clk(Clk), .clr(Reset));
  Multiplexer #(.select(2), .width(4), .enable("false")) multiplexer_2 (
    .in0(adder_1_out), .in1(subtractor_1_out), .in2(4'b1011), .in3(4'b1011), .out(multiplexer_2_out),
    .sel({Reset, xor_1_out[0]}));
  xor xor_1 (xor_1_out[0], register_1_q, or_1_out);
  Register #(.width(4)) register_2 (.D(multiplexer_2_out), .en(1'b1), .Q(register_2_q), .clk(Clk));  // open: clr
  Subtractor #(.width(4)) subtractor_1 (.a(register_2_q), .b(4'b0001), .out(subtractor_1_out));  // open: bin, bout
  Adder #(.width(4)) adder_1 (.a(register_2_q), .b(4'b0001), .out(adder_1_out));  // open: cin, cout
  or or_1 (or_1_out, comparator_2_eq, hit, comparator_1_eq);
  Comparator #(.width(4)) comparator_1 (.a(4'b1111), .b(register_2_q), .eq(comparator_1_eq));  // open: gt, lt
  Comparator #(.width(4)) comparator_2 (.a(4'b0000), .b(register_2_q), .eq(comparator_2_eq));  // open: gt, lt
  Shifter #(.width(16)) shifter_1 (.in(16'h1), .\dist (register_2_q), .out(Out));
endmodule

module Paddle_1 (
  input  Button_Down,
  input  Button_UP,
  input  Reset,
  input  [15:0] Ball_y,
  input  NearPAddle,
  output [15:0] Out,
  output Hit
);

  wire and_1_out, and_2_out, bit_extender_1_out, bit_extender_2_out, bit_extender_3_out, bit_extender_4_out,
       bit_extender_5_out, bit_extender_6_out, bit_extender_7_out, bit_extender_8_out, bit_extender_9_out,
       bit_extender_10_out, bit_extender_11_out, bit_extender_12_out, bit_extender_13_out,
       bit_extender_14_out, bit_extender_15_out, bit_extender_16_out, clock_1_out, comparator_1_eq,
       comparator_2_eq, or_1_out, or_2_out;
  wire [3:0] adder_1_out, multiplexer_1_out, multiplexer_2_out, multiplexer_3_out, register_1_q,
       subtractor_1_out;
  wire [15:0] and_3_out, and_4_out, and_5_out, and_6_out, and_7_out, and_8_out, and_9_out, and_10_out,
       and_11_out, and_12_out, and_13_out, and_14_out, and_15_out, and_16_out, and_17_out, and_18_out,
       and_19_out, and_20_out, and_21_out, and_22_out, and_23_out, and_24_out, and_25_out, and_26_out,
       and_27_out, and_28_out, and_29_out, and_30_out, and_31_out, and_32_out, and_33_out, and_34_out,
       shifter_2_out, shifter_3_out, shifter_4_out, shifter_5_out, shifter_6_out, shifter_7_out,
       shifter_8_out, shifter_9_out, shifter_10_out, shifter_11_out, shifter_12_out, shifter_13_out,
       shifter_14_out, shifter_15_out, shifter_16_out;

  Subtractor #(.width(4)) subtractor_1 (.a(register_1_q), .b(4'b0001), .out(subtractor_1_out));  // open: bin, bout
  Adder #(.width(4)) adder_1 (.a(4'b0001), .b(register_1_q), .out(adder_1_out));  // open: cin, cout
  Multiplexer #(.select(2), .width(4), .enable("false")) multiplexer_1 (
    .in0(register_1_q), .in1(subtractor_1_out), .in2(adder_1_out), .in3(register_1_q),
    .out(multiplexer_1_out), .sel({Button_UP, Button_Down}));
  Multiplexer #(.width(4), .enable("false")) multiplexer_2 (
    .in0(multiplexer_3_out), .in1(4'b0101), .out(multiplexer_2_out), .sel(Reset));
  Clock clock_1 (.out(clock_1_out));
  Register #(.width(4)) register_1 (
    .D(multiplexer_2_out), .en(1'b1), .Q(register_1_q), .clk(clock_1_out));  // open: clr
  Comparator #(.width(4)) comparator_1 (.a(4'b1100), .b(adder_1_out), .eq(comparator_1_eq));  // open: gt, lt
  Comparator #(.width(4)) comparator_2 (.a(4'b1111), .b(subtractor_1_out), .eq(comparator_2_eq));  // open: gt, lt
  Multiplexer #(.width(4), .enable("false")) multiplexer_3 (
    .in0(multiplexer_1_out), .in1(register_1_q), .out(multiplexer_3_out), .sel(or_1_out));
  or or_1 (or_1_out, and_1_out, and_2_out);
  and and_1 (and_1_out, Button_Down, comparator_2_eq);
  Shifter #(.width(16)) shifter_1 (.in(16'h1f), .\dist (register_1_q), .out(Out));
  and and_2 (and_2_out, Button_UP, comparator_1_eq);
  assign and_3_out = Out & 16'h1;  // AND_Gate and_3, 16 bits wide
  assign and_4_out = Out & 16'h2;  // AND_Gate and_4, 16 bits wide
  assign and_5_out = Out & 16'h4;  // AND_Gate and_5, 16 bits wide
  assign and_6_out = Out & 16'h8;  // AND_Gate and_6, 16 bits wide
  assign and_7_out = Out & 16'h10;  // AND_Gate and_7, 16 bits wide
  assign and_8_out = Out & 16'h20;  // AND_Gate and_8, 16 bits wide
  assign and_9_out = Out & 16'h40;  // AND_Gate and_9, 16 bits wide
  assign and_10_out = Out & 16'h80;  // AND_Gate and_10, 16 bits wide
  assign and_11_out = Out & 16'h100;  // AND_Gate and_11, 16 bits wide
  assign and_12_out = Out & 16'h200;  // AND_Gate and_12, 16 bits wide
  assign and_13_out = Out & 16'h400;  // AND_Gate and_13, 16 bits wide
  assign and_14_out = Out & 16'h800;  // AND_Gate and_14, 16 bits wide
  assign and_15_out = Out & 16'h1000;  // AND_Gate and_15, 16 bits wide
  assign and_16_out = Out & 16'h2000;  // AND_Gate and_16, 16 bits wide
  assign and_17_out = Out & 16'h4000;  // AND_Gate and_17, 16 bits wide
  assign and_18_out = Out & 16'h8000;  // AND_Gate and_18, 16 bits wide
  assign and_19_out = and_3_out & Ball_y;  // AND_Gate and_19, 16 bits wide
  assign and_20_out = and_4_out & Ball_y;  // AND_Gate and_20, 16 bits wide
  assign and_21_out = and_5_out & Ball_y;  // AND_Gate and_21, 16 bits wide
  assign and_22_out = and_6_out & Ball_y;  // AND_Gate and_22, 16 bits wide
  assign and_23_out = and_7_out & Ball_y;  // AND_Gate and_23, 16 bits wide
  assign and_24_out = and_8_out & Ball_y;  // AND_Gate and_24, 16 bits wide
  assign and_25_out = and_9_out & Ball_y;  // AND_Gate and_25, 16 bits wide
  assign and_26_out = and_10_out & Ball_y;  // AND_Gate and_26, 16 bits wide
  assign and_27_out = and_11_out & Ball_y;  // AND_Gate and_27, 16 bits wide
  assign and_28_out = and_12_out & Ball_y;  // AND_Gate and_28, 16 bits wide
  assign and_29_out = and_13_out & Ball_y;  // AND_Gate and_29, 16 bits wide
  assign and_30_out = and_14_out & Ball_y;  // AND_Gate and_30, 16 bits wide
  assign and_31_out = and_15_out & Ball_y;  // AND_Gate and_31, 16 bits wide
  assign and_32_out = and_16_out & Ball_y;  // AND_Gate and_32, 16 bits wide
  assign and_33_out = and_17_out & Ball_y;  // AND_Gate and_33, 16 bits wide
  assign and_34_out = and_18_out & Ball_y;  // AND_Gate and_34, 16 bits wide
  Shifter #(.width(16), .shift("lr")) shifter_2 (.in(and_20_out), .\dist (4'b0001), .out(shifter_2_out));
  Shifter #(.width(16), .shift("lr")) shifter_3 (.in(and_21_out), .\dist (4'b0010), .out(shifter_3_out));
  Shifter #(.width(16), .shift("lr")) shifter_4 (.in(and_22_out), .\dist (4'b0011), .out(shifter_4_out));
  Shifter #(.width(16), .shift("lr")) shifter_5 (.in(and_23_out), .\dist (4'b0100), .out(shifter_5_out));
  Shifter #(.width(16), .shift("lr")) shifter_6 (.in(and_24_out), .\dist (4'b0101), .out(shifter_6_out));
  Shifter #(.width(16), .shift("lr")) shifter_7 (.in(and_25_out), .\dist (4'b0110), .out(shifter_7_out));
  Shifter #(.width(16), .shift("lr")) shifter_8 (.in(and_26_out), .\dist (4'b0111), .out(shifter_8_out));
  Shifter #(.width(16), .shift("lr")) shifter_9 (.in(and_27_out), .\dist (4'b1000), .out(shifter_9_out));
  Shifter #(.width(16), .shift("lr")) shifter_10 (.in(and_28_out), .\dist (4'b1001), .out(shifter_10_out));
  Shifter #(.width(16), .shift("lr")) shifter_11 (.in(and_29_out), .\dist (4'b1010), .out(shifter_11_out));
  Shifter #(.width(16), .shift("lr")) shifter_12 (.in(and_30_out), .\dist (4'b1011), .out(shifter_12_out));
  Shifter #(.width(16), .shift("lr")) shifter_13 (.in(and_31_out), .\dist (4'b1100), .out(shifter_13_out));
  Shifter #(.width(16), .shift("lr")) shifter_14 (.in(and_32_out), .\dist (4'b1101), .out(shifter_14_out));
  Shifter #(.width(16), .shift("lr")) shifter_15 (.in(and_33_out), .\dist (4'b1110), .out(shifter_15_out));
  Shifter #(.width(16), .shift("lr")) shifter_16 (.in(and_34_out), .\dist (4'b1111), .out(shifter_16_out));
  Bit_Extender #(.in_width(16), .out_width(1)) bit_extender_1 (.in(and_19_out), .out(bit_extender_1_out));
  Bit_Extender #(.in_width(16), .out_width(1)) bit_extender_2 (.in(shifter_2_out), .out(bit_extender_2_out));
  Bit_Extender #(.in_width(16), .out_width(1)) bit_extender_3 (.in(shifter_3_out), .out(bit_extender_3_out));
  Bit_Extender #(.in_width(16), .out_width(1)) bit_extender_4 (.in(shifter_4_out), .out(bit_extender_4_out));
  Bit_Extender #(.in_width(16), .out_width(1)) bit_extender_5 (.in(shifter_5_out), .out(bit_extender_5_out));
  Bit_Extender #(.in_width(16), .out_width(1)) bit_extender_6 (.in(shifter_6_out), .out(bit_extender_6_out));
  Bit_Extender #(.in_width(16), .out_width(1)) bit_extender_7 (.in(shifter_7_out), .out(bit_extender_7_out));
  Bit_Extender #(.in_width(16), .out_width(1)) bit_extender_8 (.in(shifter_8_out), .out(bit_extender_8_out));
  Bit_Extender #(.in_width(16), .out_width(1)) bit_extender_9 (.in(shifter_9_out), .out(bit_extender_9_out));
  Bit_Extender #(.in_width(16), .out_width(1)) bit_extender_10 (.in(shifter_10_out), .out(bit_extender_10_out));
  Bit_Extender #(.in_width(16), .out_width(1)) bit_extender_11 (.in(shifter_11_out), .out(bit_extender_11_out));
  Bit_Extender #(.in_width(16), .out_width(1)) bit_extender_12 (.in(shifter_12_out), .out(bit_extender_12_out));
  Bit_Extender #(.in_width(16), .out_width(1)) bit_extender_13 (.in(shifter_13_out), .out(bit_extender_13_out));
  Bit_Extender #(.in_width(16), .out_width(1)) bit_extender_14 (.in(shifter_14_out), .out(bit_extender_14_out));
  Bit_Extender #(.in_width(16), .out_width(1)) bit_extender_15 (.in(shifter_15_out), .out(bit_extender_15_out));
  Bit_Extender #(.in_width(16), .out_width(1)) bit_extender_16 (.in(shifter_16_out), .out(bit_extender_16_out));
  or or_2 (or_2_out, bit_extender_1_out, bit_extender_2_out, bit_extender_3_out, bit_extender_4_out, bit_extender_5_out, bit_extender_6_out, bit_extender_7_out, bit_extender_8_out, bit_extender_9_out, bit_extender_10_out, bit_extender_11_out, bit_extender_12_out, bit_extender_13_out, bit_extender_14_out, bit_extender_15_out, bit_extender_16_out);
  and Hit_paddle (Hit, or_2_out, NearPAddle);
endmodule

module Boarder_checker (
  input  [31:0] Ball_X,
  output Hit_Boarder,
  output NearPaddle_Right,
  output NearPaddle_Left
);

  wire comparator_1_eq, comparator_2_eq;

  Comparator #(.width(32)) comparator_1 (.a(32'h80000000), .b(Ball_X), .eq(comparator_1_eq));  // open: gt, lt
  Comparator #(.width(32)) comparator_2 (.a(32'h1), .b(Ball_X), .eq(comparator_2_eq));  // open: gt, lt
  Comparator #(.width(32)) comparator_3 (.a(32'h40000000), .b(Ball_X), .eq(NearPaddle_Right));  // open: gt, lt
  Comparator #(.width(32)) comparator_4 (.a(32'h2), .b(Ball_X), .eq(NearPaddle_Left));  // open: gt, lt
  or or_1 (Hit_Boarder, comparator_1_eq, comparator_2_eq);
endmodule
